# Fritzing sketch Processing Layer (saved by Fritzing 0.8.7b)
circuit board: 5cm x 5cm
breadboards: 1
stripboards: 1

parts:
  Teensy_3_1 = Teensy 3.1
  Teensy_3_2 = Teensy 3.1
  R2 = Resistor [tolerance=±5% resistance=4.7k package=THT]
  R3 = Resistor [tolerance=±5% resistance=4.7k package=THT]

nets:
  N1: Teensy_3_1.A4/D18, Teensy_3_2.A4/D18, R2.Pin_0
  N2: Teensy_3_1.A5/D19, Teensy_3_2.A5/D19, R3.Pin_0
  3V3: Teensy_3_1.3V3, Teensy_3_2.3V3, R2.Pin_1, R3.Pin_1

notes:
  I2C
  IMU
