# Fritzing sketch Prototype 1 (saved by Fritzing 0.8.7b)
stripboards: 6
breadboards: 1

parts:
  Teensy_3_1 = Teensy 3.1  # not connected
  Teensy_3_2 = Teensy 3.1  # not connected
  CC3K1 = Adafruit CC3000 WiFi Breakout
  J1 = female pin header, 4 pins [form="♀ (female)"]
  LED1 = LED - 5mm [color="Green (560nm)" package="5 mm [THT]"]
  R2 = Resistor [tolerance=±5% resistance=4.7k package=THT]
  R3 = Resistor [tolerance=±5% resistance=4.7k package=THT]
  LED2 = RGB LED (com. anode, rbg) [package="5 mm [THT]"]
  LED3 = RGB LED (com. anode, rbg) [package="5 mm [THT]"]
  R4 = Resistor [tolerance=±5% resistance=100 package=THT]
  R5 = Resistor [tolerance=±5% resistance=100 package=THT]
  R6 = Resistor [tolerance=±5% resistance=220 package=THT]
  J2 = female pin header, 4 pins [form="♀ (female)"]
  U1 = LIPO-2000mAh [package=lipo-2000]
  U2 = LIPO-2000mAh [package=lipo-2000]

nets:
  N1: CC3K1.GND, J1.pin3, LED1.cathode, U2.-
  N2: CC3K1.VIN, U1.+
  N3: J1.pin4, R2.Pin_1, R3.Pin_1, LED2.common_anode, LED3.common_anode, J2.pin3
  N4: LED2.red_cathode, R6.Pin_0
  N5: LED2.blue_cathode, R5.Pin_0
  N6: LED2.green_cathode, R4.Pin_0
  N7: LED3.red_cathode, R6.Pin_1, J2.pin4
  N8: LED3.blue_cathode, R5.Pin_1, J2.pin2
  N9: LED3.green_cathode, R4.Pin_1, J2.pin1
  N10: U1.-, U2.+

notes:
  out port
  in port
  IMU
  RadioBlock
  I2C
  RGB LED

custom parts:
  Adafruit CC3000 WiFi Breakout: CC3000 WiFi Breakout
